# Fritzing sketch phototransistor (saved by Fritzing 1.0.3)

parts:
  U1 = raspberry_pi_pico_rp2040_1
  Q1 = phototransistor_npn_tept5600_1
  R1 = 220 Ω Resistor [Resistance=1000 package=THT]

nets:
  N1: U1.pin31, Q1.emitter, R1.Pin_0
  N2: U1.pin36, Q1.collector
  N3: U1.pin38, R1.Pin_1
