# Fritzing sketch phototransistor (saved by Fritzing 1.0.3)

parts:
  U1 = Raspberry Pi Pico (RP2040)
  Q1 = NPN Phototransistor (TEPT5600)
  R1 = 220 Ω Resistor [Resistance=1000 package=THT]

nets:
  N1: U1.Pin_31_(GP26_/_ADC0), Q1.Emitter, R1.Pin_0
  N2: U1.Pin_36_(3V3_OUT), Q1.Collector
  N3: U1.Pin_33/38_(GND_/_AGND), R1.Pin_1

custom parts:
  Raspberry Pi Pico (RP2040): Raspberry Pi Pico RP2040 microcontroller board
  NPN Phototransistor (TEPT5600): 2-lead NPN Silicon Phototransistor (Collector, Emitter)
